# Fritzing sketch Calculator_Toy (saved by Fritzing 0.9.3b)

parts:
  S7 = Momentary Switch [package=ksa_sealed_tac_switch]
  Bauteil1 = Arduino Nano (Rev3.0)
  S14 = Momentary Switch [package=ksa_sealed_tac_switch]
  S15 = Momentary Switch [package=ksa_sealed_tac_switch]
  S16 = Momentary Switch [package=ksa_sealed_tac_switch]
  S17 = Momentary Switch [package=ksa_sealed_tac_switch]
  S18 = Momentary Switch [package=ksa_sealed_tac_switch]
  S19 = Momentary Switch [package=ksa_sealed_tac_switch]
  S20 = Momentary Switch [package=ksa_sealed_tac_switch]
  S21 = Momentary Switch [package=ksa_sealed_tac_switch]
  S22 = Momentary Switch [package=ksa_sealed_tac_switch]
  S23 = Momentary Switch [package=ksa_sealed_tac_switch]
  S24 = Momentary Switch [package=ksa_sealed_tac_switch]
  Squix1 = OLED 0.96" 128x64 I2C SSD1306
  J1 = Piezo Speaker
  S32 = Round Pushbutton
  VCC3 = 4 x AAA Battery Mount
  R1 = Resistor [tolerance=±5% resistance=47k package=THT]
  R3 = Resistor [tolerance=±5% resistance=10k package=THT]
  C4 = Capacitor [package=0805]

nets:
  N1: S7.2, Bauteil1.D8, S17.2, S19.2, S22.2
  N2: S7.4, Bauteil1.D2, S15.4, S18.4
  N3: Bauteil1.D4, S19.4, S20.4, S21.4
  N4: Bauteil1.D6, S14.2, S15.2, S20.2, S23.2
  N5: Bauteil1.D7, S16.2, S18.2, S21.2, S24.2
  N6: Bauteil1.D9, S14.4, S16.4, S17.4
  N7: Bauteil1.D10, S22.4, S23.4, S24.4
  N8: Bauteil1.D11/MOSI, J1.pin2
  N9: Bauteil1.VIN, S32.leg0, R1.Pin_0
  GND: Bauteil1.GND, Squix1.GND, J1.pin1, VCC3.-, R3.Pin_1, C4.1
  5V: Bauteil1.5V, Squix1.VCC
  N10: Bauteil1.A5, Squix1.SCL
  N11: Bauteil1.A4, Squix1.SCA
  N12: Bauteil1.A0, R1.Pin_1, R3.Pin_0, C4.2
  N13: S32.leg1, VCC3.+

notes:
  Keypad layout:
  1 2 3
  4 5 6
  7 8 9
  * 0 #
  Voltage divider:
  47k | 10k + 1uF
